// Logisim project cpu.circ as structural Verilog: 1 circuit, main circuit main
module main (
  input  in_1,
  input  [7:0] in_2,
  output [7:0] out_3
);

  wire clock_1_out, comparator_1_eq, not_1_out, not_2_out;
  wire [3:0] adder_1_out, register_1_q;

  Clock clock_1 (.out(clock_1_out));
  Register #(.width(4)) register_1 (.D(adder_1_out), .en(not_1_out), .Q(register_1_q), .clk(clock_1_out));  // open: clr
  Adder #(.width(4)) adder_1 (.a(4'b0001), .b(register_1_q), .out(adder_1_out));  // open: cin, cout
  ROM #(.addrWidth(4)) rom_1 (.addr(register_1_q), .data(out_3), .sel(in_1));
  not not_1 (not_1_out, comparator_1_eq);
  Comparator comparator_1 (.a(out_3), .b(in_2), .eq(comparator_1_eq));  // open: gt, lt
  Button button_1 (.out(not_1_out));
  not not_2 (not_2_out, comparator_1_eq);
  LED led_1 (.in(not_2_out));
  LED led_2 (.in(comparator_1_eq));

  // Notes on the sheet:
  //   contents of rom_1 (hex, n*v repeats v):
  //   11 22 33 44 4*0 33 45
endmodule
